// Digital circuit 4BitAdderSubtractor.dig as structural Verilog
module _4BitAdderSubtractor (
  input  A__S,
  input  [3:0] X_3_0,
  input  [3:0] Y_3_0,
  output [3:0] S_3_0,
  output C
);

  wire fa_2_cout, fa_3_cout, fa_4_cout, xor_1_out, xor_2_out, xor_3_out, xor_4_out;

  xor xor_1 (xor_1_out, A__S, Y_3_0[3]);
  FA fa_1 (.X(X_3_0[3]), .Y(xor_1_out), .Cin(fa_2_cout), .Cout(C), .S(S_3_0[3]));
  xor xor_2 (xor_2_out, A__S, Y_3_0[2]);
  FA fa_2 (.X(X_3_0[2]), .Y(xor_2_out), .Cin(fa_3_cout), .Cout(fa_2_cout), .S(S_3_0[2]));
  xor xor_3 (xor_3_out, A__S, Y_3_0[1]);
  FA fa_3 (.X(X_3_0[1]), .Y(xor_3_out), .Cin(fa_4_cout), .Cout(fa_3_cout), .S(S_3_0[1]));
  xor xor_4 (xor_4_out, A__S, Y_3_0[0]);
  FA fa_4 (.X(X_3_0[0]), .Y(xor_4_out), .Cin(A__S), .Cout(fa_4_cout), .S(S_3_0[0]));
endmodule
