// Digital circuit test.dig as structural Verilog
module test (
  input  in_3,
  input  [3:0] in_4,
  input  [3:0] in_5,
  output out_1,
  output out_2
);

  _4BitAdderSubtractor _4bitaddersubtractor_1 (.A__S(in_3), .X_3_0(in_4), .Y_3_0(in_5));  // open: S_3_0, C
  // Pins of 1 and 4 bits meet at in_4
  // Pins of 1 and 4 bits meet at in_5
endmodule
